# Fritzing sketch 60 LED CLOCK FRITZING DESIGN (saved by Fritzing 0.8.7b)
breadboards: 1

parts:
  R1 = PHOTOCELL [package=photocell-kit]
  Part1 = Arduino Uno (Rev3)
  neopixel1 = Neopixel Ring 12
  neopixel2 = Neopixel Ring 12
  RTC1 = DS1307 RTC Breakout
  R2 = Resistor [tolerance=±5% resistance=220 package=THT]

nets:
  5V: R1.P$1, Part1.5V, neopixel1.VCC, neopixel2.VCC, RTC1.5V
  N1: R1.P$2, Part1.A3, R2.Pin_0
  N2: Part1.A4/SDA, RTC1.SDA
  N3: Part1.A5/SCL, RTC1.SCL
  N4: Part1.D9_PWM, neopixel2.IN
  N5: Part1.D10_PWM/SS, neopixel1.IN
  GND: Part1.GND, neopixel1.GND, neopixel2.GND, RTC1.GND, R2.Pin_1

notes:
  Ring 2 (60 LEDS) Minutes & Seconds
  Ring 1 (12 LEDS) Hours
  IN
  GND
  PWR

custom parts:
  Neopixel Ring 12: Neopixel Ring x12
  DS1307 RTC Breakout: DS1307 Real-time Clock Breakout Board with Battery
